// Logisim project save.circ as structural Verilog
module CONTROL_DECODER (
  input  POWER_IG,
  input  ENABLE,
  input  [3:0] SEL,
  output NO_OP,
  output ADD,
  output SUB,
  output MULTI,
  output out_8,
  output out_9,
  output out_10,
  output out_11,
  output out_12,
  output NOT,
  output AND,
  output OR,
  output XOR,
  output EQL,
  output GT,
  output LT
);

  Demultiplexer #(.select(4)) demultiplexer_1 (
    .out0(NO_OP), .out1(ADD), .out2(SUB), .out3(MULTI), .out4(out_8), .out5(out_9), .out6(out_10),
    .out7(out_11), .out8(out_12), .out9(NOT), .out10(AND), .out11(OR), .out12(XOR), .out13(EQL), .out14(GT),
    .out15(LT), .in(POWER_IG), .sel(SEL), .en(ENABLE));
endmodule

module alu (
  input  A8,
  input  A4,
  input  A2,
  input  A1,
  input  B8,
  input  B4,
  input  B2,
  input  B1,
  input  [3:0] in_9
);

  wire demultiplexer_1_out1, demultiplexer_1_out2, demultiplexer_1_out3, demultiplexer_2_out1,
       demultiplexer_2_out2, demultiplexer_2_out3, demultiplexer_3_out1, demultiplexer_3_out2,
       demultiplexer_3_out3, demultiplexer_4_out1, demultiplexer_4_out2, demultiplexer_4_out3,
       demultiplexer_5_out1, demultiplexer_5_out2, demultiplexer_5_out3, demultiplexer_6_out1,
       demultiplexer_6_out2, demultiplexer_6_out3, demultiplexer_7_out1, demultiplexer_7_out2,
       demultiplexer_7_out3, demultiplexer_8_out1, demultiplexer_8_out2, demultiplexer_8_out3;

  Demultiplexer #(.select(4)) demultiplexer_1 (
    .out1(demultiplexer_1_out1), .out2(demultiplexer_1_out2), .out3(demultiplexer_1_out3), .in(A8),
    .sel(in_9), .en(1'b1));  // open: out0, out4, out5, out6, out7, out8, out9, out10, out11, out12, out13, out14, out15
  Demultiplexer #(.select(4)) demultiplexer_2 (
    .out1(demultiplexer_2_out1), .out2(demultiplexer_2_out2), .out3(demultiplexer_2_out3), .in(A4),
    .sel(in_9), .en(1'b1));  // open: out0, out4, out5, out6, out7, out8, out9, out10, out11, out12, out13, out14, out15
  Demultiplexer #(.select(4)) demultiplexer_3 (
    .out1(demultiplexer_3_out1), .out2(demultiplexer_3_out2), .out3(demultiplexer_3_out3), .in(A2),
    .sel(in_9), .en(1'b1));  // open: out0, out4, out5, out6, out7, out8, out9, out10, out11, out12, out13, out14, out15
  Demultiplexer #(.select(4)) demultiplexer_4 (
    .out1(demultiplexer_4_out1), .out2(demultiplexer_4_out2), .out3(demultiplexer_4_out3), .in(A1),
    .sel(in_9), .en(1'b1));  // open: out0, out4, out5, out6, out7, out8, out9, out10, out11, out12, out13, out14, out15
  _4ADDER u_4adder_1 (
    .A1(demultiplexer_8_out1), .A2(demultiplexer_7_out1), .A4(demultiplexer_6_out1),
    .A8(demultiplexer_5_out1), .B1(demultiplexer_4_out1), .B2(demultiplexer_3_out1),
    .B4(demultiplexer_2_out1), .B8(demultiplexer_1_out1));  // open: in_3, AS, out_11
  _4SUB u_4sub_1 (
    .A1(demultiplexer_8_out2), .A2(demultiplexer_7_out2), .A4(demultiplexer_6_out2),
    .A8(demultiplexer_5_out2), .B1(demultiplexer_4_out2), .B2(demultiplexer_3_out2),
    .B4(demultiplexer_2_out2), .B8(demultiplexer_1_out2));  // open: in_3, SS, out_11
  _4MULT u_4mult_1 (
    .A1(demultiplexer_8_out3), .A2(demultiplexer_7_out3), .A4(demultiplexer_6_out3),
    .A8(demultiplexer_5_out3), .B1(demultiplexer_4_out3), .B2(demultiplexer_3_out3),
    .B4(demultiplexer_2_out3), .B8(demultiplexer_1_out3));  // open: in_2, out_11, MS
  Demultiplexer #(.select(4)) demultiplexer_5 (
    .out1(demultiplexer_5_out1), .out2(demultiplexer_5_out2), .out3(demultiplexer_5_out3), .in(B8),
    .sel(in_9), .en(1'b1));  // open: out0, out4, out5, out6, out7, out8, out9, out10, out11, out12, out13, out14, out15
  Demultiplexer #(.select(4)) demultiplexer_6 (
    .out1(demultiplexer_6_out1), .out2(demultiplexer_6_out2), .out3(demultiplexer_6_out3), .in(B4),
    .sel(in_9), .en(1'b1));  // open: out0, out4, out5, out6, out7, out8, out9, out10, out11, out12, out13, out14, out15
  Demultiplexer #(.select(4)) demultiplexer_7 (
    .out1(demultiplexer_7_out1), .out2(demultiplexer_7_out2), .out3(demultiplexer_7_out3), .in(B2),
    .sel(in_9), .en(1'b1));  // open: out0, out4, out5, out6, out7, out8, out9, out10, out11, out12, out13, out14, out15
  Demultiplexer #(.select(4)) demultiplexer_8 (
    .out1(demultiplexer_8_out1), .out2(demultiplexer_8_out2), .out3(demultiplexer_8_out3), .in(B1),
    .sel(in_9), .en(1'b1));  // open: out0, out4, out5, out6, out7, out8, out9, out10, out11, out12, out13, out14, out15
endmodule

module _4ADDER (
  input  A1,
  input  A2,
  input  in_3,
  input  A4,
  input  A8,
  input  B1,
  input  B2,
  input  B4,
  input  B8,
  output [3:0] AS,
  output out_11
);

  Adder #(.width(4)) adder_1 (.a({A8, A4, A2, A1}), .b({B8, B4, B2, B1}), .out(AS), .cin(in_3), .cout(out_11));
endmodule

module _4SUB (
  input  A1,
  input  A2,
  input  in_3,
  input  A4,
  input  A8,
  input  B1,
  input  B2,
  input  B4,
  input  B8,
  output [3:0] SS,
  output out_11
);

  Subtractor #(.width(4)) subtractor_1 (
    .a({A8, A4, A2, A1}), .b({B8, B4, B2, B1}), .out(SS), .bin(in_3), .bout(out_11));
endmodule

// 4MULTI
module _4MULT (
  input  A1,
  input  [3:0] in_2,
  input  A2,
  input  A4,
  input  A8,
  input  B1,
  input  B2,
  input  B4,
  input  B8,
  output [3:0] MS,
  output [3:0] out_11
);

  Multiplier #(.width(4)) multiplier_1 (
    .a({A8, A4, A2, A1}), .b({B8, B4, B2, B1}), .out(MS), .cin(in_2), .cout(out_11));
endmodule

module _16ch (
  input  [3:0] in_1,
  input  [3:0] in_2,
  output [3:0] out_3,
  output [3:0] out_4
);

  wire xor_1_out, xor_2_out, xor_3_out, xor_4_out;

  xor xor_1 (xor_1_out, in_1[2], in_2[2]);
  xor xor_2 (xor_2_out, in_1[3], in_2[3]);
  xor xor_3 (xor_3_out, in_1[1], in_2[1]);
  xor xor_4 (xor_4_out, in_1[0], in_2[0]);
endmodule

module _4NOT (
  input  _1,
  input  _2,
  input  _4,
  input  _8,
  input  ENABLE,
  output _1_2,
  output _2_2,
  output _4_2,
  output _8_2
);

  wire [3:0] not_1_out;

  assign {_8_2, _4_2, _2_2, _1_2} = ENABLE ? not_1_out : 4'bz;  // Controlled_Buffer controlled_buffer_1
  assign not_1_out = ~{_8, _4, _2, _1};  // NOT_Gate not_1, 4 bits wide
endmodule

module BITWISEDEC (
  input  [3:0] in_1
);

  wire and_1_out, nor_1_out;

  and and_1 (and_1_out, in_1[0], in_1[3]);
  // AND_Gate and_2 has open pins: in0=and_1_out, in1=nor_1_out, out=open
  nor nor_1 (nor_1_out, in_1[1], in_1[2]);
endmodule
